// Logisim project projectt.circ as structural Verilog: 31 circuits, main circuit main
// Mux5
module main (
  input  [31:0] Write,
  input  ENABLE,
  input  [23:0] Write_address,
  input  [31:0] Write_RAM,
  input  [4:0] Write_Registor_RD,
  input  store,
  output [4:0] RS,
  output [4:0] Rt,
  output [23:0] Current_PC,
  output [23:0] Next_PC,
  output [23:0] ADDRESS,
  output [4:0] RD,
  output [31:0] DATA,
  output [31:0] RS_2,
  output [31:0] Rt_2,
  output [31:0] RD_2
);

  wire alu_1_zero, and_1_out, clock_1_out, clock_2_out, clock_3_out, cu_1_alusrc, cu_1_branch, cu_1_jump,
       cu_1_jump_register, cu_1_memread, cu_1_reg_write, not_1_out, RESET_2_out, RESET_3_out, RESET_out,
       write_read_1_clock_4, write_read_1_enable_2, write_read_1_out_25, write_read_1_out_26,
       write_read_1_out_27, write_read_1_reset_3;
  wire [1:0] cu_1_alu_op, cu_1_memto_reg, cu_1_regdest;
  wire [4:0] input_select_1_out_4, mux1_1_output, wire_1_rd, write_read_1_rd_write;
  wire [5:0] wire_1_function, wire_1_opcode;
  wire [15:0] wire_1_immediate_address;
  wire [23:0] add_1_out_3, alu_1__24_bit_address, mux4_1_output, mux5_1_output, mux6_1_output,
       passthrough_ram_1_out_3, pc_1_pc_1, shiftleft2_1_out_2, shiftleft22_1_out_2, write_read_1_writeadress;
  wire [25:0] wire_1_out_2;
  wire [31:0] alu_1_alu_output, mux2_1_output, mux3_1_output, passthrough_1_out_3, ram_1_output,
       register_file_1_rd, register_file_1_rs_output, register_file_1_rt_output, rom_1_data,
       sign_ext_1__32_bits_output, write_read_1_write_output, write_read_1_write_output_2;

  pc pc_1 (
    .\input (mux6_1_output), .pc_1(pc_1_pc_1), .reset(RESET_out), .clock(clock_1_out), .adress(Current_PC),
    .pc_1_2(Next_PC));  // open: pc
  Button RESET (.out(RESET_out));
  Clock clock_1 (.out(clock_1_out));
  \wire  wire_1 (
    .Instruction_32_bits(rom_1_data), .Immediate_Address(wire_1_immediate_address),
    .Function(wire_1_function), .rd(wire_1_rd), .rt(Rt), .rs(RS), .Opcode(wire_1_opcode), .out_2(wire_1_out_2));  // open: Shamt
  ROM #(.addrWidth(24), .dataWidth(32)) rom_1 (.addr(Current_PC), .data(rom_1_data));  // open: sel
  Input_Select input_select_1 (
    .in_1(wire_1_rd), .in_2(write_read_1_rd_write), .out_4(input_select_1_out_4), .in_3(write_read_1_enable_2));
  Shiftleft2 shiftleft2_1 (.in_1(wire_1_out_2), .out_2(shiftleft2_1_out_2));
  CU cu_1 (
    .OpCode(wire_1_opcode), .Reg_Write(cu_1_reg_write), .RegDest(cu_1_regdest), .ALUSrc(cu_1_alusrc),
    .Memto_reg(cu_1_memto_reg), .MemRead(cu_1_memread), .\function (wire_1_function),
    .Jump_Register(cu_1_jump_register), .Branch(cu_1_branch), .Jump(cu_1_jump), .ALU_Op(cu_1_alu_op));
  Passthrough passthrough_1 (.in_1(mux3_1_output), .in_2(write_read_1_write_output), .out_3(passthrough_1_out_3));
  Mux1 mux1_1 (.rt(Rt), .\output (mux1_1_output), .rd(input_select_1_out_4), .a(cu_1_regdest));
  Clock clock_2 (.out(clock_2_out));
  Register_File register_file_1 (
    .Write_data(passthrough_1_out_3), .Write_Register(mux1_1_output), .regwrite(cu_1_reg_write),
    .clock(write_read_1_clock_4), .Rs(RS), .Rt(Rt), .Rs_Output(register_file_1_rs_output),
    .Rt_Output(register_file_1_rt_output), .reset(write_read_1_reset_3), .write(write_read_1_enable_2),
    .rd(register_file_1_rd));  // open: RD_Output
  Sign_Ext sign_ext_1 (.in_1(wire_1_immediate_address), ._32_bits_output(sign_ext_1__32_bits_output));
  Button RESET_2 (.out(RESET_2_out));
  Shiftleft22 shiftleft22_1 (.in_1(sign_ext_1__32_bits_output), .out_2(shiftleft22_1_out_2));
  Mux2 mux2_1 (
    .rt(register_file_1_rt_output), .\output (mux2_1_output), .rd(sign_ext_1__32_bits_output), .a(cu_1_alusrc));
  write___read write_read_1 (
    .rd_reg(mux1_1_output), .rd_reg_2(RD), .ADDRESS_Input(passthrough_ram_1_out_3), .ADDRESS(ADDRESS),
    .rd_write(write_read_1_rd_write), .enable_2(write_read_1_enable_2),
    .Write_Output(write_read_1_write_output), .reset_3(write_read_1_reset_3), .clock_4(write_read_1_clock_4),
    .RS(register_file_1_rs_output), .RT(register_file_1_rt_output), .RD(register_file_1_rd),
    .Writeadress(write_read_1_writeadress), .Write_Output_2(write_read_1_write_output_2),
    .out_25(write_read_1_out_25), .out_26(write_read_1_out_26), .out_27(write_read_1_out_27),
    .DATA(ram_1_output), .Clock(clock_1_out), .Enable(ENABLE), .Write_Registor_RD(Write_Registor_RD),
    .Write(Write), .reset_2(RESET_2_out), .clock_3(clock_2_out), .RS_2(RS_2), .Rt_2(Rt_2), .RD_2(RD_2),
    .Write_adres(Write_address), .store(store), .Write_RAM(Write_RAM), .clock_2(clock_3_out),
    .reset(RESET_3_out), .DATA_2(DATA));
  Button RESET_3 (.out(RESET_3_out));
  ADD add_1 (.in_2(pc_1_pc_1), .in_1(shiftleft22_1_out_2), .out_3(add_1_out_3));
  ALU alu_1 (
    .RS_value(register_file_1_rs_output), .RT_value(mux2_1_output), .ALU_output(alu_1_alu_output),
    .ALU_OP(cu_1_alu_op), ._24_bit_address(alu_1__24_bit_address), .zero(alu_1_zero));
  Mux4 mux4_1 (.rt(pc_1_pc_1), .\output (mux4_1_output), .a(and_1_out), .rd(add_1_out_3));
  not not_1 (not_1_out, alu_1_zero);
  and and_1 (and_1_out, not_1_out, cu_1_branch);
  passthrough_ram passthrough_ram_1 (
    .in_1(alu_1__24_bit_address), .in_2(write_read_1_writeadress), .out_3(passthrough_ram_1_out_3));
  Clock clock_3 (.out(clock_3_out));
  Mux5 mux5_1 (.rt(shiftleft2_1_out_2), .\output (mux5_1_output), .a(cu_1_jump), .rd(mux4_1_output));
  Ram ram_1 (
    .\input (passthrough_ram_1_out_3), .\output (ram_1_output), .write(write_read_1_write_output_2),
    .store(write_read_1_out_25), .clock(write_read_1_out_26), .load(cu_1_memread), .reset(write_read_1_out_27));
  Mux6 mux6_1 (.rt(mux5_1_output), .a(cu_1_jump_register), .\output (mux6_1_output), .rd(register_file_1_rs_output));
  Mux3 mux3_1 (
    .rt(alu_1_alu_output), .\output (mux3_1_output), .a(cu_1_memto_reg), .rd(ram_1_output), .in_4(pc_1_pc_1));

  // Notes on the sheet:
  //   sub v0(001) v1(110) t9(101)
  //   and t0(100)  t1(101)  t2(110)
  //   or  t0(111)  t1(101)  t2(110)
  //   addi t3(1010)  t4(101)  5
  //   lw t5(1011) 5(t6(6))
  //   bne t7(7) t8(t6(7)) 1
  //   bne t7(7) t9((5)) 1
  //   jal 4
  //   jr s0
  //   contents of rom_1 (hex, n*v repeats v):
  //   0 791022 12a4024 12a4025 218b0005 8dcd0005 15f80001 15f90001 4*0 c000004 0 0 0 2000008
  //   JumpReg
  //   J
  //   Regdst
  //   ALU op
  //   Mem to Reg
  //   Bne
  //   MemRead
  //   AluSrc
  //   RegWrite
  //   zero
  //   jr
endmodule

module ALU (
  input  [31:0] RS_value,
  input  [31:0] RT_value,
  input  [1:0] ALU_OP,
  output [31:0] ALU_output,
  output [23:0] _24_bit_address,
  output zero
);

  wire or_2_out;
  wire [31:0] adder_1_out, and_1_out, or_1_out, subtractor_1_out;

  assign and_1_out = RS_value & RT_value;  // AND_Gate and_1, 32 bits wide
  assign or_1_out = RS_value | RT_value;  // OR_Gate or_1, 32 bits wide
  Subtractor #(.width(32)) subtractor_1 (.a(RS_value), .b(RT_value), .out(subtractor_1_out));  // open: bin, bout
  Adder #(.width(32)) adder_1 (.a(RS_value), .b(RT_value), .out(adder_1_out));  // open: cin, cout
  Multiplexer #(.select(2), .width(32), .enable("false")) multiplexer_1 (
    .in0(and_1_out), .in1(or_1_out), .in2(subtractor_1_out), .in3(adder_1_out),
    .out({ALU_output[31:24], _24_bit_address}), .sel(ALU_OP));
  or or_2 (or_2_out, subtractor_1_out[0], subtractor_1_out[1], subtractor_1_out[2], subtractor_1_out[3], subtractor_1_out[4], subtractor_1_out[5], subtractor_1_out[6], subtractor_1_out[7], subtractor_1_out[8], subtractor_1_out[9], subtractor_1_out[10], subtractor_1_out[11], subtractor_1_out[12], subtractor_1_out[13], subtractor_1_out[14], subtractor_1_out[15], subtractor_1_out[17], subtractor_1_out[18], subtractor_1_out[19], subtractor_1_out[20], subtractor_1_out[21], subtractor_1_out[22], subtractor_1_out[23], subtractor_1_out[24], subtractor_1_out[25], subtractor_1_out[26], subtractor_1_out[27], subtractor_1_out[28], subtractor_1_out[29], subtractor_1_out[30], subtractor_1_out[31], subtractor_1_out[16]);
  not not_1 (zero, or_2_out);

  assign ALU_output[23:0] = _24_bit_address;
endmodule

// MUX
module Mux4 (
  input  [23:0] rt,
  input  a,
  input  [23:0] rd,
  output [23:0] \output 
);

  Multiplexer #(.width(24), .enable("false")) multiplexer_1 (.in0(rt), .in1(rd), .out(\output ), .sel(a));
endmodule

module Register_File (
  input  [4:0] Write_Register,
  input  [31:0] Write_data,
  input  regwrite,
  input  clock,
  input  reset,
  input  [4:0] Rs,
  input  [4:0] Rt,
  input  write,
  output [31:0] Rs_Output,
  output [31:0] Rt_Output,
  output [31:0] RD_Output,
  output [31:0] rd
);

  wire and_2_out, and_3_out, and_4_out, and_5_out, and_6_out, and_7_out, and_8_out, and_9_out, and_10_out,
       and_11_out, and_12_out, and_13_out, and_14_out, and_15_out, and_16_out, and_17_out, and_18_out,
       and_19_out, and_20_out, and_21_out, and_22_out, and_23_out, and_24_out, and_25_out, and_26_out,
       and_27_out, and_28_out, and_29_out, and_30_out, and_31_out, and_32_out, and_33_out, decoder_1_out0,
       decoder_1_out1, decoder_1_out2, decoder_1_out3, decoder_1_out4, decoder_1_out5, decoder_1_out6,
       decoder_1_out7, decoder_1_out8, decoder_1_out9, decoder_1_out10, decoder_1_out11, decoder_1_out12,
       decoder_1_out13, decoder_1_out14, decoder_1_out15, decoder_1_out16, decoder_1_out17, decoder_1_out18,
       decoder_1_out19, decoder_1_out20, decoder_1_out21, decoder_1_out22, decoder_1_out23, decoder_1_out24,
       decoder_1_out25, decoder_1_out26, decoder_1_out27, decoder_1_out28, decoder_1_out29, decoder_1_out30,
       decoder_1_out31;
  wire [31:0] multiplexer_3_out, register_1_q, register_2_q, register_3_q, register_4_q, register_5_q,
       register_6_q, register_7_q, register_8_q, register_9_q, register_10_q, register_11_q, register_12_q,
       register_13_q, register_14_q, register_15_q, register_16_q, register_17_q, register_18_q,
       register_19_q, register_20_q, register_21_q, register_22_q, register_23_q, register_24_q,
       register_25_q, register_26_q, register_27_q, register_28_q, register_29_q, register_30_q,
       register_31_q, register_32_q;
  wire [31:31] not_1_out;

  not not_1 (not_1_out[31], write);
  assign RD_Output = Write_data & {32{not_1_out[31]}};  // AND_Gate and_1, 32 bits wide
  and and_2 (and_2_out, decoder_1_out0, regwrite);
  and and_3 (and_3_out, decoder_1_out1, regwrite);
  and and_4 (and_4_out, decoder_1_out2, regwrite);
  and and_5 (and_5_out, decoder_1_out3, regwrite);
  and and_6 (and_6_out, decoder_1_out4, regwrite);
  and and_7 (and_7_out, decoder_1_out5, regwrite);
  and and_8 (and_8_out, decoder_1_out6, regwrite);
  and and_9 (and_9_out, decoder_1_out7, regwrite);
  and and_10 (and_10_out, decoder_1_out8, regwrite);
  and and_11 (and_11_out, decoder_1_out9, regwrite);
  and and_12 (and_12_out, decoder_1_out10, regwrite);
  and and_13 (and_13_out, decoder_1_out11, regwrite);
  and and_14 (and_14_out, decoder_1_out12, regwrite);
  and and_15 (and_15_out, decoder_1_out13, regwrite);
  and and_16 (and_16_out, decoder_1_out14, regwrite);
  and and_17 (and_17_out, decoder_1_out15, regwrite);
  Decoder #(.select(5)) decoder_1 (
    .out0(decoder_1_out0), .out1(decoder_1_out1), .out2(decoder_1_out2), .out3(decoder_1_out3),
    .out4(decoder_1_out4), .out5(decoder_1_out5), .out6(decoder_1_out6), .out7(decoder_1_out7),
    .out8(decoder_1_out8), .out9(decoder_1_out9), .out10(decoder_1_out10), .out11(decoder_1_out11),
    .out12(decoder_1_out12), .out13(decoder_1_out13), .out14(decoder_1_out14), .out15(decoder_1_out15),
    .out16(decoder_1_out16), .out17(decoder_1_out17), .out18(decoder_1_out18), .out19(decoder_1_out19),
    .out20(decoder_1_out20), .out21(decoder_1_out21), .out22(decoder_1_out22), .out23(decoder_1_out23),
    .out24(decoder_1_out24), .out25(decoder_1_out25), .out26(decoder_1_out26), .out27(decoder_1_out27),
    .out28(decoder_1_out28), .out29(decoder_1_out29), .out30(decoder_1_out30), .out31(decoder_1_out31),
    .sel(Write_Register));  // open: en
  Register #(.width(32)) register_1 (.D(Write_data), .en(and_2_out), .Q(register_1_q), .clk(clock), .clr(reset));
  Register #(.width(32)) register_2 (.D(Write_data), .en(and_3_out), .Q(register_2_q), .clk(clock), .clr(reset));
  Register #(.width(32)) register_3 (.D(Write_data), .en(and_4_out), .Q(register_3_q), .clk(clock), .clr(reset));
  Register #(.width(32)) register_4 (.D(Write_data), .en(and_5_out), .Q(register_4_q), .clk(clock), .clr(reset));
  Register #(.width(32)) register_5 (.D(Write_data), .en(and_6_out), .Q(register_5_q), .clk(clock), .clr(reset));
  Register #(.width(32)) register_6 (.D(Write_data), .en(and_7_out), .Q(register_6_q), .clk(clock), .clr(reset));
  Register #(.width(32)) register_7 (.D(Write_data), .en(and_8_out), .Q(register_7_q), .clk(clock), .clr(reset));
  Register #(.width(32)) register_8 (.D(Write_data), .en(and_9_out), .Q(register_8_q), .clk(clock), .clr(reset));
  Register #(.width(32)) register_9 (.D(Write_data), .en(and_10_out), .Q(register_9_q), .clk(clock), .clr(reset));
  Register #(.width(32)) register_10 (.D(Write_data), .en(and_11_out), .Q(register_10_q), .clk(clock), .clr(reset));
  Register #(.width(32)) register_11 (.D(Write_data), .en(and_12_out), .Q(register_11_q), .clk(clock), .clr(reset));
  Register #(.width(32)) register_12 (.D(Write_data), .en(and_13_out), .Q(register_12_q), .clk(clock), .clr(reset));
  Register #(.width(32)) register_13 (.D(Write_data), .en(and_14_out), .Q(register_13_q), .clk(clock), .clr(reset));
  Register #(.width(32)) register_14 (.D(Write_data), .en(and_15_out), .Q(register_14_q), .clk(clock), .clr(reset));
  Register #(.width(32)) register_15 (.D(Write_data), .en(and_16_out), .Q(register_15_q), .clk(clock), .clr(reset));
  Register #(.width(32)) register_16 (.D(Write_data), .en(and_17_out), .Q(register_16_q), .clk(clock), .clr(reset));
  and and_18 (and_18_out, decoder_1_out31, regwrite);
  and and_19 (and_19_out, decoder_1_out30, regwrite);
  and and_20 (and_20_out, decoder_1_out29, regwrite);
  and and_21 (and_21_out, decoder_1_out28, regwrite);
  and and_22 (and_22_out, decoder_1_out27, regwrite);
  and and_23 (and_23_out, decoder_1_out26, regwrite);
  and and_24 (and_24_out, decoder_1_out25, regwrite);
  and and_25 (and_25_out, decoder_1_out24, regwrite);
  and and_26 (and_26_out, decoder_1_out23, regwrite);
  and and_27 (and_27_out, decoder_1_out22, regwrite);
  and and_28 (and_28_out, decoder_1_out21, regwrite);
  and and_29 (and_29_out, decoder_1_out20, regwrite);
  and and_30 (and_30_out, decoder_1_out19, regwrite);
  and and_31 (and_31_out, decoder_1_out18, regwrite);
  and and_32 (and_32_out, decoder_1_out17, regwrite);
  and and_33 (and_33_out, decoder_1_out16, regwrite);
  Register #(.width(32)) register_17 (.D(Write_data), .en(and_18_out), .Q(register_17_q), .clk(clock), .clr(reset));
  Register #(.width(32)) register_18 (.D(Write_data), .en(and_19_out), .Q(register_18_q), .clk(clock), .clr(reset));
  Register #(.width(32)) register_19 (.D(Write_data), .en(and_20_out), .Q(register_19_q), .clk(clock), .clr(reset));
  Register #(.width(32)) register_20 (.D(Write_data), .en(and_21_out), .Q(register_20_q), .clk(clock), .clr(reset));
  Register #(.width(32)) register_21 (.D(Write_data), .en(and_22_out), .Q(register_21_q), .clk(clock), .clr(reset));
  Register #(.width(32)) register_22 (.D(Write_data), .en(and_23_out), .Q(register_22_q), .clk(clock), .clr(reset));
  Register #(.width(32)) register_23 (.D(Write_data), .en(and_24_out), .Q(register_23_q), .clk(clock), .clr(reset));
  Register #(.width(32)) register_24 (.D(Write_data), .en(and_25_out), .Q(register_24_q), .clk(clock), .clr(reset));
  Register #(.width(32)) register_25 (.D(Write_data), .en(and_26_out), .Q(register_25_q), .clk(clock), .clr(reset));
  Register #(.width(32)) register_26 (.D(Write_data), .en(and_27_out), .Q(register_26_q), .clk(clock), .clr(reset));
  Register #(.width(32)) register_27 (.D(Write_data), .en(and_28_out), .Q(register_27_q), .clk(clock), .clr(reset));
  Register #(.width(32)) register_28 (.D(Write_data), .en(and_29_out), .Q(register_28_q), .clk(clock), .clr(reset));
  Register #(.width(32)) register_29 (.D(Write_data), .en(and_30_out), .Q(register_29_q), .clk(clock), .clr(reset));
  Register #(.width(32)) register_30 (.D(Write_data), .en(and_31_out), .Q(register_30_q), .clk(clock), .clr(reset));
  Register #(.width(32)) register_31 (.D(Write_data), .en(and_32_out), .Q(register_31_q), .clk(clock), .clr(reset));
  Register #(.width(32)) register_32 (.D(Write_data), .en(and_33_out), .Q(register_32_q), .clk(clock), .clr(reset));
  pass pass_1 (.in_1(Write_Register), .N(Write_data), .in_3(multiplexer_3_out), .out_4(rd));
  Multiplexer #(.select(5), .width(32)) multiplexer_1 (
    .in0(register_1_q), .in1(register_2_q), .in2(register_3_q), .in3(register_4_q), .in4(register_5_q),
    .in5(register_6_q), .in6(register_7_q), .in7(register_8_q), .in8(register_9_q), .in9(register_10_q),
    .in10(register_11_q), .in11(register_12_q), .in12(register_13_q), .in13(register_14_q),
    .in14(register_15_q), .in15(register_16_q), .in16(register_32_q), .in17(register_31_q),
    .in18(register_30_q), .in19(register_29_q), .in20(register_28_q), .in21(register_27_q),
    .in22(register_26_q), .in23(register_25_q), .in24(register_24_q), .in25(register_23_q),
    .in26(register_22_q), .in27(register_21_q), .in28(register_20_q), .in29(register_19_q),
    .in30(register_18_q), .in31(register_17_q), .out(Rs_Output), .sel(Rs));  // open: en
  Multiplexer #(.select(5), .width(32)) multiplexer_2 (
    .in0(register_1_q), .in1(register_2_q), .in2(register_3_q), .in3(register_4_q), .in4(register_5_q),
    .in5(register_6_q), .in6(register_7_q), .in7(register_8_q), .in8(register_9_q), .in9(register_10_q),
    .in10(register_11_q), .in11(register_12_q), .in12(register_13_q), .in13(register_14_q),
    .in14(register_15_q), .in15(register_16_q), .in16(register_32_q), .in17(register_31_q),
    .in18(register_30_q), .in19(register_29_q), .in20(register_28_q), .in21(register_27_q),
    .in22(register_26_q), .in23(register_25_q), .in24(register_24_q), .in25(register_23_q),
    .in26(register_22_q), .in27(register_21_q), .in28(register_20_q), .in29(register_19_q),
    .in30(register_18_q), .in31(register_17_q), .out(Rt_Output), .sel(Rt));  // open: en
  Multiplexer #(.select(5), .width(32)) multiplexer_3 (
    .in0(register_1_q), .in1(register_2_q), .in2(register_3_q), .in3(register_4_q), .in4(register_5_q),
    .in5(register_6_q), .in6(register_7_q), .in7(register_8_q), .in8(register_9_q), .in9(register_10_q),
    .in10(register_11_q), .in11(register_12_q), .in12(register_13_q), .in13(register_14_q),
    .in14(register_15_q), .in15(register_16_q), .in16(register_32_q), .in17(register_31_q),
    .in18(register_30_q), .in19(register_29_q), .in20(register_28_q), .in21(register_27_q),
    .in22(register_26_q), .in23(register_25_q), .in24(register_24_q), .in25(register_23_q),
    .in26(register_22_q), .in27(register_21_q), .in28(register_20_q), .in29(register_19_q),
    .in30(register_18_q), .in31(register_17_q), .out(multiplexer_3_out), .sel(Write_Register));  // open: en
endmodule

// MUX
module Mux1 (
  input  [4:0] rt,
  input  [4:0] rd,
  input  [1:0] a,
  output [4:0] \output 
);

  Multiplexer #(.select(2), .width(5), .enable("false")) multiplexer_1 (
    .in0(rt), .in2({5{1'b1}}), .in3(rd), .out(\output ), .sel(a));  // open: in1
endmodule

// CONTROL UNIT
module CU (
  input  [5:0] OpCode,
  input  [5:0] \function ,
  output Reg_Write,
  output [1:0] RegDest,
  output ALUSrc,
  output [1:0] Memto_reg,
  output MemRead,
  output Branch,
  output Jump,
  output Jump_Register,
  output [1:0] ALU_Op
);

  wire and_2_out, and_5_out, and_7_out, and_8_out, not_1_out, not_2_out, not_4_out, or_1_out, or_3_out,
       xor_3_out;
  wire [0:0] xor_1_out;
  wire [1:0] or_4_out;
  wire [1:1] or_2_out;

  or or_1 (or_1_out, OpCode[0], OpCode[1], OpCode[2], OpCode[3], OpCode[4], OpCode[5]);
  and and_1 (MemRead, OpCode[0], OpCode[1], and_2_out);
  and and_2 (and_2_out, OpCode[0], OpCode[1], OpCode[5]);
  and and_3 (Branch, OpCode[0], OpCode[2]);
  and and_4 (Jump, OpCode[0], OpCode[1], not_1_out);
  not not_1 (not_1_out, OpCode[5]);
  and and_5 (and_5_out, OpCode[3], 1'b1);
  not not_2 (not_2_out, or_1_out);
  not not_3 (RegDest[0], or_1_out);
  or or_2 (or_2_out[1], and_2_out, and_5_out);
  or or_3 (or_3_out, not_2_out, and_2_out);
  and and_6 (ALUSrc, or_1_out, not_4_out);
  and and_7 (and_7_out, not_4_out, or_1_out);
  not not_4 (not_4_out, Branch);
  and and_8 (and_8_out, 1'b1, Branch);
  xor xor_1 (xor_1_out[0], Branch, and_8_out);
  assign or_4_out = {2{or_2_out[1]}} | \function [1:0];  // OR_Gate or_4, 2 bits wide
  assign ALU_Op = {Branch, xor_1_out[0]} | or_4_out;  // OR_Gate or_5, 2 bits wide
  or or_6 (Reg_Write, OpCode[3], or_3_out);
  xor xor_2 (RegDest[1], RegDest[0], Jump);
  xor xor_3 (xor_3_out, and_7_out, OpCode[3]);
  xor xor_4 (Memto_reg[1], Jump, xor_3_out);

  assign Jump_Register = \function [3];
  assign Memto_reg[0] = Jump;
endmodule

// SignExt
module Sign_Ext (
  input  [15:0] in_1,
  output [31:0] _32_bits_output
);


  assign _32_bits_output = {{16{1'b0}}, in_1};
endmodule

// ALU Control
module ALU_C (
  input  [5:0] Function,
  output [1:0] ALU_Op
);


  assign ALU_Op = Function[1:0];
endmodule

// MUX
module Mux2 (
  input  [31:0] rt,
  input  a,
  input  [31:0] rd,
  output [31:0] \output 
);

  Multiplexer #(.width(32), .enable("false")) multiplexer_1 (.in0(rt), .in1(rd), .out(\output ), .sel(a));
endmodule

module Shiftleft2 (
  input  [25:0] in_1,
  output [23:0] out_2
);


  assign out_2 = {in_1[21:0], 2'b00};
endmodule

// MUX
module Mux3 (
  input  [31:0] rt,
  input  [1:0] a,
  input  [31:0] rd,
  input  [23:0] in_4,
  output [31:0] \output 
);

  Multiplexer #(.select(2), .width(32), .enable("false")) multiplexer_1 (
    .in0(rt), .in1({{8{1'b0}}, in_4}), .in2(rd), .out(\output ), .sel(a));  // open: in3
endmodule

// MUX
module Mux5 (
  input  [23:0] rt,
  input  a,
  input  [23:0] rd,
  output [23:0] \output 
);

  Multiplexer #(.width(24), .enable("false")) multiplexer_1 (.in0(rd), .in1(rt), .out(\output ), .sel(a));
endmodule

module ADD (
  input  [23:0] in_1,
  input  [23:0] in_2,
  output [23:0] out_3
);

  Adder #(.width(24)) adder_1 (.a(in_1), .b(in_2), .out(out_3), .cin(1'b0));  // open: cout
endmodule

// MUX
module Mux6 (
  input  [23:0] rt,
  input  a,
  input  [31:0] rd,
  output [23:0] \output 
);

  Multiplexer #(.width(24), .enable("false")) multiplexer_1 (.in0(rt), .in1(rd[23:0]), .out(\output ), .sel(a));
endmodule

module loop (
  input  [23:0] in_1,
  output out_2
);

  and and_1 (out_2, in_1[3], in_1[0]);
endmodule

module \wire  (
  input  [31:0] Instruction_32_bits,
  output [25:0] out_2,
  output [5:0] Function,
  output [4:0] Shamt,
  output [4:0] rd,
  output [4:0] rt,
  output [4:0] rs,
  output [5:0] Opcode,
  output [15:0] Immediate_Address
);

  wire not_1_out, or_1_out;

  not not_1 (not_1_out, or_1_out);
  or or_1 (or_1_out, Instruction_32_bits[31], Instruction_32_bits[29], Instruction_32_bits[30], Instruction_32_bits[28], Instruction_32_bits[27], Instruction_32_bits[26]);
  and and_1 (Function[5], Instruction_32_bits[5], not_1_out);
  and and_2 (Function[4], Instruction_32_bits[4], not_1_out);
  and and_3 (Function[3], Instruction_32_bits[3], not_1_out);
  and and_4 (Function[1], Instruction_32_bits[1], not_1_out);
  and and_5 (Function[2], Instruction_32_bits[2], not_1_out);
  and and_6 (Function[0], Instruction_32_bits[0], not_1_out);

  assign Immediate_Address = Instruction_32_bits[15:0];
  assign Opcode = Instruction_32_bits[31:26];
  assign out_2 = Instruction_32_bits[25:0];
  assign rd = Instruction_32_bits[15:11];
  assign rs = Instruction_32_bits[25:21];
  assign rt = Instruction_32_bits[20:16];
  assign Shamt = Instruction_32_bits[10:6];
endmodule

module test (
  input  in_1,
  input  [31:0] in_2,
  input  [4:0] in_3,
  input  [4:0] in_4,
  input  [4:0] in_5,
  input  [4:0] in_6,
  input  [4:0] in_7,
  input  [4:0] in_8,
  input  in_9,
  input  in_10,
  input  [4:0] in_11,
  output [31:0] out_12,
  output [31:0] out_13,
  output [4:0] out_14,
  output [4:0] out_15
);

  wire clock_1_out;
  wire [4:0] and_1_out, and_2_out;
  wire [4:4] not_1_out;

  not not_1 (not_1_out[4], in_10);
  assign and_1_out = in_6 & {5{not_1_out[4]}};  // AND_Gate and_1, 5 bits wide
  assign and_2_out = in_8 & {5{in_10}};  // AND_Gate and_2, 5 bits wide
  Clock clock_1 (.out(clock_1_out));
  assign out_14 = and_1_out | and_2_out;  // OR_Gate or_1, 5 bits wide
  // Register_File register_file_1: pin names not known; wires that end beside it: in_2, in_3, in_4, in_5, in_1, clock_1_out, out_12, out_13
  Input_Select input_select_1 (.in_1(in_7), .in_2(in_11), .out_4(out_15), .in_3(in_9));
  Mux1 mux1_1 (.rd(out_15));  // open: rt, output, a
endmodule

module Passthrough (
  input  [31:0] in_1,
  input  [31:0] in_2,
  output [31:0] out_3
);

  assign out_3 = in_1 | in_2;  // OR_Gate or_1, 32 bits wide
endmodule

module passthrough2 (
  input  in_1,
  input  in_2,
  output clock
);

  wire or_1_out;

  not not_1 (clock, or_1_out);
  or or_1 (or_1_out, in_1, in_2);
endmodule

module display (
  input  [31:0] in_1,
  output [3:0] out_2,
  output [3:0] out_3,
  output [3:0] out_4,
  output [3:0] out_5,
  output [3:0] out_6,
  output [3:0] out_7,
  output [3:0] out_8,
  output [3:0] out_9
);


  assign out_2 = in_1[3:0];
  assign out_3 = in_1[7:4];
  assign out_4 = in_1[11:8];
  assign out_5 = in_1[15:12];
  assign out_6 = in_1[19:16];
  assign out_7 = in_1[23:20];
  assign out_8 = in_1[27:24];
  assign out_9 = in_1[31:28];
endmodule

// Shiftleft2
module Shiftleft22 (
  input  [31:0] in_1,
  output [23:0] out_2
);


  assign out_2 = {in_1[21:0], 2'b00};
endmodule

// J
module jump (
  input  [23:0] in_1,
  input  [23:0] in_2,
  output [23:0] out_3
);

  Adder #(.width(24)) adder_1 (.a(in_1), .b(in_2), .out(out_3));  // open: cin, cout
endmodule

module Input_Select (
  input  [4:0] in_1,
  input  [4:0] in_2,
  input  in_3,
  output [4:0] out_4
);

  wire [4:0] and_1_out, and_2_out;
  wire [4:4] not_1_out;

  not not_1 (not_1_out[4], in_3);
  assign and_1_out = in_1 & {5{not_1_out[4]}};  // AND_Gate and_1, 5 bits wide
  assign and_2_out = in_2 & {5{in_3}};  // AND_Gate and_2, 5 bits wide
  assign out_4 = and_1_out | and_2_out;  // OR_Gate or_1, 5 bits wide
endmodule

// RAM
module Ram (
  input  [23:0] \input ,
  input  [31:0] write,
  input  store,
  input  clock,
  input  load,
  input  reset,
  output [31:0] \output 
);

  RAM #(.addrWidth(24), .dataWidth(32), .bus("separate")) ram_1 (
    .addr(\input ), .din(write), .data(\output ), .str(store), .clk(clock), .ld(load), .clr(reset));  // open: sel
endmodule

// PC
module pc (
  input  [23:0] \input ,
  input  reset,
  input  clock,
  output [23:0] pc,
  output [23:0] pc_1,
  output [23:0] adress,
  output [23:0] pc_1_2
);

  Adder #(.width(24)) adder_1 (.a(24'h1), .b(adress), .out(pc_1), .cin(1'b0));  // open: cout
  Register #(.width(24)) register_1 (.D(\input ), .en(1'b1), .Q(adress), .clk(clock), .clr(reset));

  assign pc = adress;
  assign pc_1_2 = \input ;
endmodule

module input_select_write (
  input  [31:0] in_1,
  input  in_2,
  output [31:0] out_3
);

  assign out_3 = in_1 & {32{in_2}};  // AND_Gate and_1, 32 bits wide
endmodule

module passthrough_ram (
  input  [23:0] in_1,
  input  [23:0] in_2,
  output [23:0] out_3
);

  assign out_3 = in_1 | in_2;  // OR_Gate or_1, 24 bits wide
endmodule

// WRITE & READ
module write___read (
  input  [4:0] rd_reg,
  input  [31:0] RS,
  input  [31:0] RT,
  input  [31:0] RD,
  input  [31:0] DATA,
  input  [23:0] ADDRESS_Input,
  input  Clock,
  input  store,
  input  clock_2,
  input  reset,
  input  [31:0] Write_RAM,
  input  [23:0] Write_adres,
  input  Enable,
  input  [31:0] Write,
  input  [4:0] Write_Registor_RD,
  input  reset_2,
  input  clock_3,
  output [4:0] rd_write,
  output [23:0] Writeadress,
  output [31:0] Write_Output,
  output [31:0] Write_Output_2,
  output enable_2,
  output reset_3,
  output clock_4,
  output out_25,
  output out_26,
  output out_27,
  output [31:0] DATA_2,
  output [23:0] ADDRESS,
  output [4:0] rd_reg_2,
  output [31:0] RS_2,
  output [31:0] Rt_2,
  output [31:0] RD_2
);

  input_select_write input_select_write_1 (.in_1(Write), .out_3(Write_Output), .in_2(Enable));
  passthrough2 passthrough2_1 (.in_1(Clock), .in_2(clock_3), .clock(clock_4));
  assign Writeadress = {24{store}} & Write_adres;  // AND_Gate and_1, 24 bits wide
  passthrouhg_3 passthrouhg_3_1 (.in_1(Clock), .in_2(clock_2), .clock(out_26));

  assign ADDRESS = ADDRESS_Input;
  assign DATA_2 = DATA;
  assign enable_2 = Enable;
  assign out_25 = store;
  assign out_27 = reset;
  assign RD_2 = RD;
  assign rd_reg_2 = rd_reg;
  assign rd_write = Write_Registor_RD;
  assign reset_3 = reset_2;
  assign RS_2 = RS;
  assign Rt_2 = RT;
  assign Write_Output_2 = Write_RAM;
endmodule

module tests (
  input  [5:0] Opcode,
  input  [5:0] Function,
  output out_3,
  output out_4,
  output [1:0] out_5,
  output [1:0] out_6,
  output out_7,
  output out_8,
  output out_9,
  output out_10,
  output [1:0] out_11
);

  CU cu_1 (
    .OpCode(Opcode), .Reg_Write(out_10), .RegDest(out_11), .ALUSrc(out_9), .Memto_reg(out_6),
    .MemRead(out_8), .\function (Function), .Jump_Register(out_3), .Branch(out_7), .Jump(out_4),
    .ALU_Op(out_5));

  // Notes on the sheet:
  //   bne
  //   JumpReg
  //   JAL
  //   ALU op
  //   Mem to Reg
  //   Bne
  //   MemRead
  //   Regdst
  //   AluSrc
  //   RegWrite
  //   00 = AND
  //   01 = OR
  //   11 = ADD
  //   ALU
  //   10 = SUBTRACT
endmodule

module passthrouhg_3 (
  input  in_1,
  input  in_2,
  output clock
);

  or or_1 (clock, in_1, in_2);
endmodule

module pass (
  input  [4:0] in_1,
  input  [31:0] N,
  input  [31:0] in_3,
  output [31:0] out_4
);

  wire [31:0] and_2_out, and_3_out, not_1_out;
  wire [31:31] and_1_out;

  and and_1 (and_1_out[31], in_1[0], in_1[1], in_1[2], in_1[3], in_1[4]);
  assign not_1_out = ~{32{and_1_out[31]}};  // NOT_Gate not_1, 32 bits wide
  assign and_2_out = {32{and_1_out[31]}} & N;  // AND_Gate and_2, 32 bits wide
  assign and_3_out = not_1_out & in_3;  // AND_Gate and_3, 32 bits wide
  assign out_4 = and_2_out | and_3_out;  // OR_Gate or_1, 32 bits wide
endmodule
